// Logisim project 9Floor_Elevator.circ as structural Verilog
module main (
);

  wire _1el, _2el, _3el, _4el, _5el, _6el, _7el, _8el, c1el, c2el, c3el, c4el, c5el, c6el, c7el, c8el,
       call1r, call1st1_q, call1st2_q, call2nd1_q, call2nd2_q, call2r, call3r, call3rd1_q, call3rd2_q,
       call4r, call4th1_q, call4th2_q, call5r, call5th1_q, call5th2_q, call6r, call6th1_q, call6th2_q,
       call7r, call7th1_q, call7th2_q, call8r, call8th1_q, call8th2_q, call_1st_out, call_2nd_out,
       call_3rd_out, call_4th_out, call_5th_out, call_6th_out, call_7th_out, call_8th_out, call_ground_out,
       callgr, callGr1_q, callGr2_q, cgel, clock, Final_1, Final_2, Final_3, Final_4, Final_5, Final_6,
       Final_7, Final_8, Final_G, g1el, g2el, g3el, g4el, g5el, g6el, g7el, g8el, gel, ggel, go1r, go1st1_q,
       go1st2_q, go2nd1_q, go2nd2_q, go2r, go3r, go3rd1_q, go3rd2_q, go4r, go4th1_q, go4th2_q, go5r,
       go5th1_q, go5th2_q, go6r, go6th1_q, go6th2_q, go7r, go7th1_q, go7th2_q, go7th_2_out, go8r, go8th1_q,
       go8th2_q, go_1st_out, go_2nd_out, go_3rd_out, go_4th_out, go_5th_out, go_6th_out, go_8th_out,
       go_ground_out, gogr, goGr1_q, goGr2_q, not_1_out, not_2_out, not_3_out, not_4_out, not_5_out,
       not_6_out, not_7_out, not_8_out, not_9_out, not_10_out, not_11_out, not_12_out, not_13_out,
       not_14_out, not_15_out, not_16_out, not_17_out, not_18_out, not_19_out, not_20_out, not_21_out,
       not_22_out, not_23_out, not_24_out, not_25_out, not_26_out, not_27_out, not_28_out, not_29_out,
       not_30_out, not_31_out, not_32_out, not_33_out, not_34_out, not_35_out, not_36_out, not_37_out,
       not_38_out, not_39_out, not_40_out, not_41_out, not_42_out, not_43_out, not_44_out, not_45_out,
       not_46_out, not_47_out, not_48_out, not_49_out, not_50_out, not_51_out, not_52_out, not_53_out,
       not_54_out, not_55_out, not_56_out, not_57_out, not_58_out, not_59_out, not_60_out, not_61_out,
       not_62_out, not_63_out, not_64_out, not_65_out, not_66_out, not_67_out, not_68_out, not_69_out,
       not_70_out, not_71_out, not_72_out, not_73_out, not_74_out, not_75_out, not_76_out, not_77_out,
       not_78_out, not_79_out, not_80_out, not_81_out, not_82_out, not_83_out, not_84_out, not_85_out,
       not_86_out, not_87_out, not_88_out, not_89_out, not_90_out, not_91_out, not_92_out, not_93_out,
       not_94_out, not_95_out, not_96_out, not_97_out, not_98_out, not_99_out, not_100_out, not_101_out,
       not_102_out, not_103_out, not_104_out, not_105_out, not_106_out, not_107_out, not_108_out,
       not_109_out, not_110_out, not_111_out, not_112_out, not_113_out, not_114_out, not_115_out,
       not_116_out, not_117_out, not_118_out, not_119_out, not_120_out, not_121_out, not_122_out,
       not_123_out, not_124_out, not_125_out, not_126_out, not_127_out, not_128_out, not_129_out,
       not_130_out, not_131_out, not_132_out, not_133_out, not_134_out, not_135_out, not_136_out,
       not_137_out, not_138_out, not_139_out, not_140_out, not_141_out, not_142_out, not_143_out,
       not_144_out, not_145_out, not_146_out, not_147_out, not_148_out, not_149_out, not_150_out,
       not_151_out, not_152_out, not_153_out, not_154_out, not_155_out, not_156_out, not_157_out,
       not_158_out, not_159_out, not_160_out, not_161_out, not_162_out, not_163_out, not_164_out,
       not_165_out, not_166_out, not_167_out, not_168_out, not_169_out, not_170_out, not_171_out,
       not_172_out, not_173_out, not_174_out, not_175_out, not_176_out, not_177_out, not_178_out,
       not_179_out, not_180_out, not_181_out, not_182_out, not_183_out, not_184_out, not_185_out,
       not_186_out, not_187_out, not_188_out, not_189_out, not_190_out, not_191_out, not_192_out,
       not_193_out, not_194_out, not_195_out, not_196_out, not_197_out, not_198_out, not_199_out,
       not_200_out, not_201_out, not_202_out, not_203_out, not_204_out, not_205_out, not_206_out,
       not_207_out, not_208_out, not_209_out, not_210_out, not_211_out, not_212_out, not_213_out,
       not_214_out, not_215_out, not_216_out;
  wire [3:0] table_1_x1;

  Clock clock_1 (.out(clock));
  D_Flip_Flop ground_floor (.clk(clock), .D(Final_G), .Q(gel));  // open: Qn, preset, en, reset
  D_Flip_Flop _1st_floor (.clk(clock), .D(Final_1), .Q(_1el));  // open: Qn, preset, en, reset
  D_Flip_Flop _2nd_floor (.clk(clock), .D(Final_2), .Q(_2el));  // open: Qn, preset, en, reset
  D_Flip_Flop _3rd_floor (.clk(clock), .D(Final_3), .Q(_3el));  // open: Qn, preset, en, reset
  D_Flip_Flop _4th_floor (.clk(clock), .D(Final_4), .Q(_4el));  // open: Qn, preset, en, reset
  D_Flip_Flop _5th_floor (.clk(clock), .D(Final_5), .Q(_5el));  // open: Qn, preset, en, reset
  D_Flip_Flop _6th_floor (.clk(clock), .D(Final_6), .Q(_6el));  // open: Qn, preset, en, reset
  D_Flip_Flop _7th_floor (.clk(clock), .D(Final_7), .Q(_7el));  // open: Qn, preset, en, reset
  D_Flip_Flop _8th_floor (.clk(clock), .D(Final_8), .Q(_8el));  // open: Qn, preset, en, reset
  not not_1 (not_1_out, _8el);
  not not_2 (not_2_out, gel);
  not not_3 (not_3_out, _1el);
  not not_4 (not_4_out, _2el);
  not not_5 (not_5_out, _3el);
  not not_6 (not_6_out, _5el);
  not not_7 (not_7_out, _6el);
  not not_8 (not_8_out, _7el);
  not not_9 (not_9_out, _8el);
  not not_10 (not_10_out, c8el);
  not not_11 (not_11_out, c7el);
  not not_12 (not_12_out, c6el);
  not not_13 (not_13_out, c5el);
  not not_14 (not_14_out, c3el);
  not not_15 (not_15_out, c2el);
  not not_16 (not_16_out, g8el);
  not not_17 (not_17_out, g7el);
  not not_18 (not_18_out, g6el);
  not not_19 (not_19_out, g5el);
  not not_20 (not_20_out, g3el);
  not not_21 (not_21_out, g2el);
  not not_22 (not_22_out, g1el);
  not not_23 (not_23_out, ggel);
  not not_24 (not_24_out, _1el);
  not not_25 (not_25_out, _2el);
  not not_26 (not_26_out, _3el);
  not not_27 (not_27_out, _4el);
  not not_28 (not_28_out, _5el);
  not not_29 (not_29_out, _6el);
  not not_30 (not_30_out, _7el);
  not not_31 (not_31_out, c8el);
  not not_32 (not_32_out, c7el);
  not not_33 (not_33_out, c6el);
  not not_34 (not_34_out, c5el);
  not not_35 (not_35_out, c4el);
  not not_36 (not_36_out, c3el);
  not not_37 (not_37_out, g8el);
  not not_38 (not_38_out, g7el);
  not not_39 (not_39_out, g6el);
  not not_40 (not_40_out, g5el);
  not not_41 (not_41_out, g4el);
  not not_42 (not_42_out, g3el);
  not not_43 (not_43_out, g2el);
  not not_44 (not_44_out, g1el);
  not not_45 (not_45_out, c1el);
  not not_46 (not_46_out, cgel);
  not not_47 (not_47_out, c2el);
  not not_48 (not_48_out, c1el);
  D_Flip_Flop call8th2 (.clk(clock), .D(call8th1_q), .Q(call8th2_q));  // open: Qn, preset, en, reset
  or call8th (c8el, call8th2_q, call8th1_q);
  D_Flip_Flop call8th1 (.clk(clock), .D(call8r), .Q(call8th1_q));  // open: Qn, preset, en, reset
  D_Flip_Flop call7th2 (.clk(clock), .D(call7th1_q), .Q(call7th2_q));  // open: Qn, preset, en, reset
  or call7th (c7el, call7th2_q, call7th1_q);
  D_Flip_Flop call7th1 (.clk(clock), .D(call7r), .Q(call7th1_q));  // open: Qn, preset, en, reset
  D_Flip_Flop call6th2 (.clk(clock), .D(call6th1_q), .Q(call6th2_q));  // open: Qn, preset, en, reset
  or call6th (c6el, call6th2_q, call6th1_q);
  D_Flip_Flop call6th1 (.clk(clock), .D(call6r), .Q(call6th1_q));  // open: Qn, preset, en, reset
  D_Flip_Flop call5th2 (.clk(clock), .D(call5th1_q), .Q(call5th2_q));  // open: Qn, preset, en, reset
  or call5th (c5el, call5th2_q, call5th1_q);
  D_Flip_Flop call5th1 (.clk(clock), .D(call5r), .Q(call5th1_q));  // open: Qn, preset, en, reset
  D_Flip_Flop call4th2 (.clk(clock), .D(call4th1_q), .Q(call4th2_q));  // open: Qn, preset, en, reset
  or call4th (c4el, call4th2_q, call4th1_q);
  D_Flip_Flop call4th1 (.clk(clock), .D(call4r), .Q(call4th1_q));  // open: Qn, preset, en, reset
  D_Flip_Flop call3rd2 (.clk(clock), .D(call3rd1_q), .Q(call3rd2_q));  // open: Qn, preset, en, reset
  or call3rd (c3el, call3rd2_q, call3rd1_q);
  D_Flip_Flop call3rd1 (.clk(clock), .D(call3r), .Q(call3rd1_q));  // open: Qn, preset, en, reset
  D_Flip_Flop call2nd2 (.clk(clock), .D(call2nd1_q), .Q(call2nd2_q));  // open: Qn, preset, en, reset
  or call2nd (c2el, call2nd2_q, call2nd1_q);
  D_Flip_Flop call2nd1 (.clk(clock), .D(call2r), .Q(call2nd1_q));  // open: Qn, preset, en, reset
  D_Flip_Flop call1st2 (.clk(clock), .D(call1st1_q), .Q(call1st2_q));  // open: Qn, preset, en, reset
  or call1st (c1el, call1st2_q, call1st1_q);
  D_Flip_Flop call1st1 (.clk(clock), .D(call1r), .Q(call1st1_q));  // open: Qn, preset, en, reset
  D_Flip_Flop callGr2 (.clk(clock), .D(callGr1_q), .Q(callGr2_q));  // open: Qn, preset, en, reset
  or u_callGr (cgel, callGr2_q, callGr1_q);
  D_Flip_Flop callGr1 (.clk(clock), .D(callgr), .Q(callGr1_q));  // open: Qn, preset, en, reset
  and and_1 (Final_G, not_24_out, not_25_out, not_26_out, not_27_out, not_28_out, not_29_out, not_30_out, not_1_out, not_31_out, not_32_out, not_33_out, not_34_out, not_35_out, not_36_out, not_47_out, not_48_out, not_37_out, not_38_out, not_39_out, not_40_out, not_41_out, not_42_out, not_43_out, not_44_out);
  and and_2 (Final_4, not_2_out, not_3_out, not_4_out, not_5_out, not_6_out, not_7_out, not_8_out, not_9_out, not_10_out, not_11_out, not_12_out, not_13_out, not_14_out, not_15_out, not_45_out, not_46_out, not_16_out, not_17_out, not_18_out, not_19_out, not_20_out, not_21_out, not_22_out, not_23_out);
  D_Flip_Flop go8th2 (.clk(clock), .D(go8th1_q), .Q(go8th2_q));  // open: Qn, preset, en, reset
  D_Flip_Flop go8th1 (.clk(clock), .D(go8r), .Q(go8th1_q));  // open: Qn, preset, en, reset
  D_Flip_Flop go7th2 (.clk(clock), .D(go7th1_q), .Q(go7th2_q));  // open: Qn, preset, en, reset
  D_Flip_Flop go7th1 (.clk(clock), .D(go7r), .Q(go7th1_q));  // open: Qn, preset, en, reset
  D_Flip_Flop go6th2 (.clk(clock), .D(go6th1_q), .Q(go6th2_q));  // open: Qn, preset, en, reset
  D_Flip_Flop go6th1 (.clk(clock), .D(go6r), .Q(go6th1_q));  // open: Qn, preset, en, reset
  D_Flip_Flop go5th2 (.clk(clock), .D(go5th1_q), .Q(go5th2_q));  // open: Qn, preset, en, reset
  D_Flip_Flop go5th1 (.clk(clock), .D(go5r), .Q(go5th1_q));  // open: Qn, preset, en, reset
  D_Flip_Flop go4th2 (.clk(clock), .D(go4th1_q), .Q(go4th2_q));  // open: Qn, preset, en, reset
  D_Flip_Flop go4th1 (.clk(clock), .D(go4r), .Q(go4th1_q));  // open: Qn, preset, en, reset
  D_Flip_Flop go3rd2 (.clk(clock), .D(go3rd1_q), .Q(go3rd2_q));  // open: Qn, preset, en, reset
  D_Flip_Flop go3rd1 (.clk(clock), .D(go3r), .Q(go3rd1_q));  // open: Qn, preset, en, reset
  D_Flip_Flop go2nd2 (.clk(clock), .D(go2nd1_q), .Q(go2nd2_q));  // open: Qn, preset, en, reset
  D_Flip_Flop go2nd1 (.clk(clock), .D(go2r), .Q(go2nd1_q));  // open: Qn, preset, en, reset
  D_Flip_Flop go1st2 (.clk(clock), .D(go1st1_q), .Q(go1st2_q));  // open: Qn, preset, en, reset
  D_Flip_Flop go1st1 (.clk(clock), .D(go1r), .Q(go1st1_q));  // open: Qn, preset, en, reset
  D_Flip_Flop goGr2 (.clk(clock), .D(goGr1_q), .Q(goGr2_q));  // open: Qn, preset, en, reset
  D_Flip_Flop goGr1 (.clk(clock), .D(gogr), .Q(goGr1_q));  // open: Qn, preset, en, reset
  not not_49 (not_49_out, gel);
  not not_50 (not_50_out, _1el);
  not not_51 (not_51_out, _2el);
  not not_52 (not_52_out, _3el);
  not not_53 (not_53_out, _4el);
  not not_54 (not_54_out, _6el);
  not not_55 (not_55_out, _7el);
  not not_56 (not_56_out, _8el);
  not not_57 (not_57_out, c8el);
  not not_58 (not_58_out, c7el);
  not not_59 (not_59_out, c6el);
  not not_60 (not_60_out, c4el);
  not not_61 (not_61_out, c3el);
  not not_62 (not_62_out, g8el);
  not not_63 (not_63_out, g7el);
  not not_64 (not_64_out, g6el);
  not not_65 (not_65_out, g4el);
  not not_66 (not_66_out, g3el);
  not not_67 (not_67_out, g2el);
  not not_68 (not_68_out, g1el);
  not not_69 (not_69_out, ggel);
  or go8th (g8el, go8th2_q, go8th1_q);
  or go7th (g7el, go7th2_q, go7th1_q);
  or go6th (g6el, go6th2_q, go6th1_q);
  or go5th (g5el, go5th2_q, go5th1_q);
  or go4th (g4el, go4th2_q, go4th1_q);
  or go3rd (g3el, go3rd2_q, go3rd1_q);
  or go2nd (g2el, go2nd2_q, go2nd1_q);
  or go1st (g1el, go1st2_q, go1st1_q);
  or u_goGr (ggel, goGr2_q, goGr1_q);
  not not_70 (not_70_out, gel);
  not not_71 (not_71_out, _2el);
  not not_72 (not_72_out, _3el);
  not not_73 (not_73_out, _4el);
  not not_74 (not_74_out, _5el);
  not not_75 (not_75_out, _6el);
  not not_76 (not_76_out, _7el);
  not not_77 (not_77_out, _8el);
  not not_78 (not_78_out, c8el);
  not not_79 (not_79_out, c7el);
  not not_80 (not_80_out, c6el);
  not not_81 (not_81_out, c5el);
  not not_82 (not_82_out, c4el);
  not not_83 (not_83_out, g8el);
  not not_84 (not_84_out, g7el);
  not not_85 (not_85_out, g6el);
  not not_86 (not_86_out, g5el);
  not not_87 (not_87_out, g4el);
  not not_88 (not_88_out, g3el);
  not not_89 (not_89_out, g2el);
  not not_90 (not_90_out, ggel);
  not not_91 (not_91_out, c2el);
  not not_92 (not_92_out, c1el);
  not not_93 (not_93_out, cgel);
  not not_94 (not_94_out, c3el);
  not not_95 (not_95_out, c2el);
  not not_96 (not_96_out, cgel);
  LED G (.in(Final_G));
  and and_3 (Final_5, not_49_out, not_50_out, not_51_out, not_52_out, not_53_out, not_54_out, not_55_out, not_56_out, not_57_out, not_58_out, not_59_out, not_60_out, not_61_out, not_91_out, not_92_out, not_93_out, not_62_out, not_63_out, not_64_out, not_65_out, not_66_out, not_67_out, not_68_out, not_69_out);
  LED _2 (.in(Final_2));
  LED _3 (.in(Final_3));
  LED _1 (.in(Final_1));
  LED _4 (.in(Final_4));
  and and_4 (Final_1, not_70_out, not_71_out, not_72_out, not_73_out, not_74_out, not_75_out, not_76_out, not_77_out, not_78_out, not_79_out, not_80_out, not_81_out, not_82_out, not_94_out, not_95_out, not_96_out, not_83_out, not_84_out, not_85_out, not_86_out, not_87_out, not_88_out, not_89_out, not_90_out);
  LED _7 (.in(Final_7));
  LED _8 (.in(Final_8));
  LED _5 (.in(Final_5));
  LED _6 (.in(Final_6));
  not not_97 (not_97_out, gel);
  not not_98 (not_98_out, _1el);
  not not_99 (not_99_out, _2el);
  not not_100 (not_100_out, _3el);
  not not_101 (not_101_out, _4el);
  not not_102 (not_102_out, _5el);
  not not_103 (not_103_out, _7el);
  not not_104 (not_104_out, _8el);
  not not_105 (not_105_out, c8el);
  not not_106 (not_106_out, c7el);
  not not_107 (not_107_out, c5el);
  not not_108 (not_108_out, c4el);
  not not_109 (not_109_out, c3el);
  not not_110 (not_110_out, g8el);
  not not_111 (not_111_out, g7el);
  not not_112 (not_112_out, g5el);
  not not_113 (not_113_out, g4el);
  not not_114 (not_114_out, g3el);
  not not_115 (not_115_out, g2el);
  not not_116 (not_116_out, g1el);
  not not_117 (not_117_out, ggel);
  Hex_Digit_Display hex_digit_display_1 (.value(table_1_x1));  // open: dp
  Table table_1 (
    .f8(Final_8), .f7(Final_7), .f6(Final_6), .f5(Final_5), .f4(Final_4), .f3(Final_3), .f2(Final_2),
    .f1(Final_1), .f0(Final_G), .x4(table_1_x1[3]), .x3(table_1_x1[2]), .x2(table_1_x1[1]), .x1(table_1_x1[0]));
  not not_118 (not_118_out, _8el);
  not not_119 (not_119_out, c2el);
  not not_120 (not_120_out, c1el);
  not not_121 (not_121_out, cgel);
  not not_122 (not_122_out, gel);
  not not_123 (not_123_out, _1el);
  not not_124 (not_124_out, _3el);
  not not_125 (not_125_out, _4el);
  not not_126 (not_126_out, _5el);
  not not_127 (not_127_out, _6el);
  not not_128 (not_128_out, _7el);
  not not_129 (not_129_out, c8el);
  not not_130 (not_130_out, c7el);
  not not_131 (not_131_out, c6el);
  not not_132 (not_132_out, c5el);
  not not_133 (not_133_out, c4el);
  not not_134 (not_134_out, c3el);
  not not_135 (not_135_out, g8el);
  not not_136 (not_136_out, g7el);
  not not_137 (not_137_out, g6el);
  not not_138 (not_138_out, g5el);
  not not_139 (not_139_out, g4el);
  not not_140 (not_140_out, g3el);
  not not_141 (not_141_out, g1el);
  not not_142 (not_142_out, ggel);
  not not_143 (not_143_out, c1el);
  not not_144 (not_144_out, cgel);
  and and_5 (Final_6, not_97_out, not_98_out, not_99_out, not_100_out, not_101_out, not_102_out, not_103_out, not_104_out, not_105_out, not_106_out, not_107_out, not_108_out, not_109_out, not_119_out, not_120_out, not_121_out, not_110_out, not_111_out, not_112_out, not_113_out, not_114_out, not_115_out, not_116_out, not_117_out);
  and and_6 (Final_2, not_122_out, not_123_out, not_124_out, not_125_out, not_126_out, not_127_out, not_128_out, not_118_out, not_129_out, not_130_out, not_131_out, not_132_out, not_133_out, not_134_out, not_143_out, not_144_out, not_135_out, not_136_out, not_137_out, not_138_out, not_139_out, not_140_out, not_141_out, not_142_out);
  not not_145 (not_145_out, gel);
  not not_146 (not_146_out, _1el);
  not not_147 (not_147_out, _2el);
  not not_148 (not_148_out, _3el);
  not not_149 (not_149_out, _4el);
  not not_150 (not_150_out, _5el);
  not not_151 (not_151_out, _6el);
  not not_152 (not_152_out, _8el);
  not not_153 (not_153_out, c8el);
  not not_154 (not_154_out, c6el);
  not not_155 (not_155_out, c5el);
  not not_156 (not_156_out, c4el);
  not not_157 (not_157_out, c3el);
  not not_158 (not_158_out, g8el);
  not not_159 (not_159_out, g6el);
  not not_160 (not_160_out, g5el);
  not not_161 (not_161_out, g4el);
  not not_162 (not_162_out, g3el);
  not not_163 (not_163_out, g2el);
  not not_164 (not_164_out, g1el);
  not not_165 (not_165_out, ggel);
  not not_166 (not_166_out, c2el);
  not not_167 (not_167_out, c1el);
  not not_168 (not_168_out, cgel);
  Button go_8th (.out(go_8th_out));
  Button go7th_2 (.out(go7th_2_out));
  Button go_6th (.out(go_6th_out));
  Button go_5th (.out(go_5th_out));
  Button go_4th (.out(go_4th_out));
  Button go_3rd (.out(go_3rd_out));
  Button go_2nd (.out(go_2nd_out));
  Button go_1st (.out(go_1st_out));
  Button go_ground (.out(go_ground_out));
  Button call_8th (.out(call_8th_out));
  Button call_7th (.out(call_7th_out));
  Button call_6th (.out(call_6th_out));
  Button call_5th (.out(call_5th_out));
  Button call_4th (.out(call_4th_out));
  Button call_3rd (.out(call_3rd_out));
  Button call_2nd (.out(call_2nd_out));
  Button call_1st (.out(call_1st_out));
  Button call_ground (.out(call_ground_out));
  not not_169 (not_169_out, gel);
  not not_170 (not_170_out, _1el);
  not not_171 (not_171_out, _2el);
  not not_172 (not_172_out, _4el);
  not not_173 (not_173_out, _5el);
  not not_174 (not_174_out, _6el);
  not not_175 (not_175_out, _7el);
  not not_176 (not_176_out, _8el);
  not not_177 (not_177_out, c8el);
  not not_178 (not_178_out, c7el);
  not not_179 (not_179_out, c6el);
  not not_180 (not_180_out, c5el);
  not not_181 (not_181_out, g8el);
  not not_182 (not_182_out, g7el);
  not not_183 (not_183_out, g6el);
  not not_184 (not_184_out, g5el);
  not not_185 (not_185_out, g4el);
  not not_186 (not_186_out, g2el);
  not not_187 (not_187_out, g1el);
  not not_188 (not_188_out, ggel);
  and and_7 (Final_7, not_145_out, not_146_out, not_147_out, not_148_out, not_149_out, not_150_out, not_151_out, not_152_out, not_153_out, not_154_out, not_155_out, not_156_out, not_157_out, not_166_out, not_167_out, not_168_out, not_158_out, not_159_out, not_160_out, not_161_out, not_162_out, not_163_out, not_164_out, not_165_out);
  buttons buttons_1 (
    .g8i(go_8th_out), .g7i(go7th_2_out), .g6i(go_6th_out), .g5i(go_5th_out), .g4i(go_4th_out),
    .g3i(go_3rd_out), .g2i(go_2nd_out), .g1i(go_1st_out), .ggi(go_ground_out), .c8i(call_8th_out),
    .c7i(call_7th_out), .c6i(call_6th_out), .c5i(call_5th_out), .c4i(call_4th_out), .c3i(call_3rd_out),
    .c2i(call_2nd_out), .c1i(call_1st_out), .cgi(call_ground_out), .g8o(go8r), .g7o(go7r), .g6o(go6r),
    .g5o(go5r), .g4o(go4r), .g3o(go3r), .g2o(go2r), .g1o(go1r), .ggo(gogr), .c8o(call8r), .c7o(call7r),
    .c6o(call6r), .c5o(call5r), .c4o(call4r), .c3o(call3r), .c2o(call2r), .c1o(call1r), .cgo(callgr));
  not not_189 (not_189_out, c4el);
  not not_190 (not_190_out, c2el);
  not not_191 (not_191_out, c1el);
  not not_192 (not_192_out, cgel);
  not not_193 (not_193_out, gel);
  not not_194 (not_194_out, _1el);
  not not_195 (not_195_out, _2el);
  not not_196 (not_196_out, _3el);
  not not_197 (not_197_out, _4el);
  not not_198 (not_198_out, _5el);
  not not_199 (not_199_out, _6el);
  not not_200 (not_200_out, _7el);
  not not_201 (not_201_out, c7el);
  not not_202 (not_202_out, c6el);
  not not_203 (not_203_out, c5el);
  not not_204 (not_204_out, c4el);
  not not_205 (not_205_out, c3el);
  not not_206 (not_206_out, g7el);
  not not_207 (not_207_out, g6el);
  not not_208 (not_208_out, g5el);
  not not_209 (not_209_out, g4el);
  not not_210 (not_210_out, g3el);
  not not_211 (not_211_out, g2el);
  not not_212 (not_212_out, g1el);
  not not_213 (not_213_out, ggel);
  and and_8 (Final_3, not_169_out, not_170_out, not_171_out, not_172_out, not_173_out, not_174_out, not_175_out, not_176_out, not_177_out, not_178_out, not_179_out, not_180_out, not_189_out, not_190_out, not_191_out, not_192_out, not_181_out, not_182_out, not_183_out, not_184_out, not_185_out, not_186_out, not_187_out, not_188_out);
  not not_214 (not_214_out, c2el);
  not not_215 (not_215_out, c1el);
  not not_216 (not_216_out, cgel);
  and and_9 (Final_8, not_193_out, not_194_out, not_195_out, not_196_out, not_197_out, not_198_out, not_199_out, not_200_out, not_201_out, not_202_out, not_203_out, not_204_out, not_205_out, not_214_out, not_215_out, not_216_out, not_206_out, not_207_out, not_208_out, not_209_out, not_210_out, not_211_out, not_212_out, not_213_out);

  // Notes on the sheet:
  //   outside
  //   cabin
  //   LEDs
  //   Display
  //   cabin
  //   outside
endmodule

module buttons (
  input  g8i,
  input  g7i,
  input  g6i,
  input  g5i,
  input  g4i,
  input  g3i,
  input  g2i,
  input  g1i,
  input  ggi,
  input  c8i,
  input  c7i,
  input  c6i,
  input  c5i,
  input  c4i,
  input  c3i,
  input  c2i,
  input  c1i,
  input  cgi,
  output g8o,
  output g7o,
  output g6o,
  output g5o,
  output g4o,
  output g3o,
  output g2o,
  output g1o,
  output ggo,
  output c8o,
  output c7o,
  output c6o,
  output c5o,
  output c4o,
  output c3o,
  output c2o,
  output c1o,
  output cgo
);

  wire clock_1_out;

  D_Flip_Flop d_ff_1 (.Q(g5o), .preset(g5i), .reset(clock_1_out));  // open: clk, D, Qn, en
  D_Flip_Flop d_ff_2 (.Q(c8o), .preset(c8i), .reset(clock_1_out));  // open: clk, D, Qn, en
  D_Flip_Flop d_ff_3 (.Q(c3o), .preset(c3i), .reset(clock_1_out));  // open: clk, D, Qn, en
  D_Flip_Flop d_ff_4 (.Q(g6o), .preset(g6i), .reset(clock_1_out));  // open: clk, D, Qn, en
  D_Flip_Flop d_ff_5 (.Q(g2o), .preset(g2i), .reset(clock_1_out));  // open: clk, D, Qn, en
  D_Flip_Flop d_ff_6 (.Q(ggo), .preset(ggi), .reset(clock_1_out));  // open: clk, D, Qn, en
  D_Flip_Flop d_ff_7 (.Q(c6o), .preset(c6i), .reset(clock_1_out));  // open: clk, D, Qn, en
  D_Flip_Flop d_ff_8 (.Q(c4o), .preset(c4i), .reset(clock_1_out));  // open: clk, D, Qn, en
  D_Flip_Flop d_ff_9 (.Q(c1o), .preset(c1i), .reset(clock_1_out));  // open: clk, D, Qn, en
  D_Flip_Flop d_ff_10 (.Q(cgo), .preset(cgi), .reset(clock_1_out));  // open: clk, D, Qn, en
  D_Flip_Flop d_ff_11 (.Q(g8o), .preset(g8i), .reset(clock_1_out));  // open: clk, D, Qn, en
  Clock clock_1 (.out(clock_1_out));
  D_Flip_Flop d_ff_12 (.Q(g7o), .preset(g7i), .reset(clock_1_out));  // open: clk, D, Qn, en
  D_Flip_Flop d_ff_13 (.Q(g4o), .preset(g4i), .reset(clock_1_out));  // open: clk, D, Qn, en
  D_Flip_Flop d_ff_14 (.Q(g1o), .preset(g1i), .reset(clock_1_out));  // open: clk, D, Qn, en
  D_Flip_Flop d_ff_15 (.Q(c7o), .preset(c7i), .reset(clock_1_out));  // open: clk, D, Qn, en
  D_Flip_Flop d_ff_16 (.Q(c5o), .preset(c5i), .reset(clock_1_out));  // open: clk, D, Qn, en
  D_Flip_Flop d_ff_17 (.Q(g3o), .preset(g3i), .reset(clock_1_out));  // open: clk, D, Qn, en
  D_Flip_Flop d_ff_18 (.Q(c2o), .preset(c2i), .reset(clock_1_out));  // open: clk, D, Qn, en

  // Notes on the sheet:
  //   go 8th
  //   go 7th
  //   go 6th
  //   go 5th
  //   go 4th
  //   go 3rd
  //   go 2nd
  //   go 1st
  //   go ground
  //   call 8th
  //   call 7th
  //   call 6th
  //   call 5th
  //   call 4th
  //   call 3rd
  //   call 2nd
  //   call 1st
  //   call ground
  //   call 6th
  //   call 3rd
  //   go 5th
  //   go 3rd
  //   go 2nd
  //   call 8th
  //   call 4th
  //   go 4th
  //   go ground
  //   call 7th
  //   call 5th
  //   call 1st
  //   call ground
  //   go 1st
  //   call 2nd
  //   go 8th
  //   go 7th
  //   go 6th
endmodule

module Table (
  input  f8,
  input  f7,
  input  f6,
  input  f5,
  input  f4,
  input  f3,
  input  f2,
  input  f1,
  input  f0,
  output x4,
  output x3,
  output x2,
  output x1
);

  wire nand_1_out, nand_2_out, nand_3_out, nand_4_out, nand_5_out, nand_6_out, nand_7_out, nand_8_out,
       nand_9_out, nand_10_out, nand_11_out, nand_12_out, nand_13_out, nand_14_out, nand_15_out, nand_16_out,
       nand_17_out, nand_18_out, nand_19_out, nand_20_out, nand_21_out, nand_22_out, nand_23_out,
       nand_24_out, nand_25_out, nand_26_out, nand_27_out, nand_28_out, nand_29_out, nand_30_out,
       nand_31_out, nand_32_out, nand_33_out, nand_34_out, nand_35_out, nand_36_out, nand_37_out,
       nand_38_out, nand_39_out, nand_40_out, nand_41_out, nand_42_out, nand_43_out, nand_44_out,
       nand_45_out, nand_46_out, nand_47_out, nand_48_out, nand_49_out, nand_50_out, nand_51_out,
       nand_52_out, nand_53_out, nand_54_out, nand_55_out, nand_56_out, nand_57_out, nand_58_out,
       nand_59_out, nand_60_out, nand_61_out, nand_62_out, nand_63_out, nand_64_out, nand_65_out,
       nand_66_out, nand_67_out, nand_68_out, nand_69_out, nand_70_out, nand_71_out, nand_72_out;

  nand nand_1 (nand_1_out, f8, f8);
  nand nand_2 (nand_2_out, f3, f3);
  nand nand_3 (nand_3_out, f2, f2);
  nand nand_4 (nand_4_out, f1, f1);
  nand nand_5 (nand_5_out, f0, f0);
  nand nand_6 (nand_6_out, f8, f8);
  nand nand_7 (nand_7_out, f3, f3);
  nand nand_8 (nand_8_out, f2, f2);
  nand nand_9 (nand_9_out, f1, f1);
  nand nand_10 (nand_10_out, f0, f0);
  nand nand_11 (nand_11_out, f8, f8);
  nand nand_12 (nand_12_out, f3, f3);
  nand nand_13 (nand_13_out, f2, f2);
  nand nand_14 (nand_14_out, f1, f1);
  nand nand_15 (nand_15_out, f0, f0);
  nand nand_16 (nand_16_out, f8, f8);
  nand nand_17 (nand_17_out, f3, f3);
  nand nand_18 (nand_18_out, f2, f2);
  nand nand_19 (nand_19_out, f1, f1);
  nand nand_20 (nand_20_out, f0, f0);
  nand nand_21 (nand_21_out, f8, f8);
  nand nand_22 (nand_22_out, f5, f5);
  nand nand_23 (nand_23_out, f4, f4);
  nand nand_24 (nand_24_out, f1, f1);
  nand nand_25 (nand_25_out, f0, f0);
  nand nand_26 (nand_26_out, f8, f8);
  nand nand_27 (nand_27_out, f5, f5);
  nand nand_28 (nand_28_out, f4, f4);
  nand nand_29 (nand_29_out, f1, f1);
  nand nand_30 (nand_30_out, f0, f0);
  nand nand_31 (nand_31_out, f8, f8);
  nand nand_32 (nand_32_out, f5, f5);
  nand nand_33 (nand_33_out, f4, f4);
  nand nand_34 (nand_34_out, f1, f1);
  nand nand_35 (nand_35_out, f0, f0);
  nand nand_36 (nand_36_out, f8, f8);
  nand nand_37 (nand_37_out, f5, f5);
  nand nand_38 (nand_38_out, f4, f4);
  nand nand_39 (nand_39_out, f1, f1);
  nand nand_40 (nand_40_out, f0, f0);
  nand nand_41 (nand_41_out, f8, f8);
  nand nand_42 (nand_42_out, f6, f6);
  nand nand_43 (nand_43_out, f4, f4);
  nand nand_44 (nand_44_out, f2, f2);
  nand nand_45 (nand_45_out, f0, f0);
  nand nand_46 (nand_46_out, f8, f8);
  nand nand_47 (nand_47_out, f6, f6);
  nand nand_48 (nand_48_out, f4, f4);
  nand nand_49 (nand_49_out, f2, f2);
  nand nand_50 (nand_50_out, f0, f0);
  nand nand_51 (nand_51_out, f8, f8);
  nand nand_52 (nand_52_out, f6, f6);
  nand nand_53 (nand_53_out, f4, f4);
  nand nand_54 (nand_54_out, f2, f2);
  nand nand_55 (nand_55_out, f0, f0);
  nand nand_56 (nand_56_out, f8, f8);
  nand nand_57 (nand_57_out, f6, f6);
  nand nand_58 (nand_58_out, f4, f4);
  nand nand_59 (nand_59_out, f2, f2);
  nand nand_60 (nand_60_out, f0, f0);
  nand nand_61 (nand_61_out, nand_1_out, f4, nand_2_out, nand_3_out, nand_4_out, nand_5_out);
  nand nand_62 (nand_62_out, nand_6_out, f5, nand_7_out, nand_8_out, nand_9_out, nand_10_out);
  nand nand_63 (nand_63_out, nand_11_out, f6, nand_12_out, nand_13_out, nand_14_out, nand_15_out);
  nand nand_64 (nand_64_out, nand_16_out, f7, nand_17_out, nand_18_out, nand_19_out, nand_20_out);
  nand nand_65 (nand_65_out, nand_21_out, nand_22_out, nand_23_out, f2, nand_24_out, nand_25_out);
  nand nand_66 (nand_66_out, nand_26_out, nand_27_out, nand_28_out, f3, nand_29_out, nand_30_out);
  nand nand_67 (nand_67_out, nand_31_out, f6, nand_32_out, nand_33_out, nand_34_out, nand_35_out);
  nand nand_68 (nand_68_out, nand_36_out, f7, nand_37_out, nand_38_out, nand_39_out, nand_40_out);
  nand nand_69 (nand_69_out, nand_41_out, nand_42_out, nand_43_out, nand_44_out, f1, nand_45_out);
  nand nand_70 (nand_70_out, nand_46_out, nand_47_out, nand_48_out, f3, nand_49_out, nand_50_out);
  nand nand_71 (nand_71_out, nand_51_out, nand_52_out, f5, nand_53_out, nand_54_out, nand_55_out);
  nand nand_72 (nand_72_out, nand_56_out, f7, nand_57_out, nand_58_out, nand_59_out, nand_60_out);
  nand nand_73 (x3, nand_61_out, nand_62_out, nand_63_out, nand_64_out);
  nand nand_74 (x2, nand_65_out, nand_66_out, nand_67_out, nand_68_out);
  nand nand_75 (x1, nand_69_out, nand_70_out, nand_71_out, nand_72_out);

  assign x4 = f8;
endmodule
